# Fritzing sketch Sensori_I2C_pcf8574 (saved by Fritzing 0.9.3b)
circuit board: 5.14352cm x 4.74338cm
perfboards: 1

parts:
  U1 = PCF8574 [package="DIP16 [THT]"]
  R1 = Resistor [tolerance=±5% resistance=10k package=THT]
  R2 = Resistor [tolerance=±5% resistance=10k package=THT]
  R3 = Resistor [tolerance=±5% resistance=10k package=THT]
  J3 = Screw terminal - 2 pins [package=THT]
  J4 = Screw terminal - 2 pins [package=THT]
  J5 = Screw terminal - 2 pins [package=THT]
  J6 = Screw terminal - 2 pins [package=THT]
  J7 = Screw terminal - 2 pins [package=THT]
  J8 = Screw terminal - 2 pins [package=THT]
  J9 = Screw terminal - 2 pins [package=THT]
  J10 = Screw terminal - 2 pins [package=THT]
  J11 = Screw terminal - 2 pins [package=THT]
  J12 = Screw terminal - 2 pins [package=THT]
  R4 = Resistor [tolerance=±5% resistance=10k package=THT]
  R5 = Resistor [tolerance=±5% resistance=10k package=THT]
  R6 = Resistor [tolerance=±5% resistance=10k package=THT]
  R7 = Resistor [tolerance=±5% resistance=10k package=THT]
  R9 = Resistor [tolerance=±5% resistance=10k package=THT]
  R10 = Resistor [tolerance=±5% resistance=10k package=THT]
  R11 = Resistor [tolerance=±5% resistance=10k package=THT]
  R12 = Resistor [tolerance=±5% resistance=10k package=THT]
  R13 = Resistor [tolerance=±5% resistance=10k package=THT]
  J13 = male pin header, 2 pins [form="♂ (male)"]
  J17 = male pin header, 2 pins [form="♂ (male)"]
  J20 = male pin header, 2 pins [form="♂ (male)"]
  J21 = male pin header, 2 pins [form="♂ (male)"]
  J22 = male pin header, 2 pins [form="♂ (male)"]
  J23 = male pin header, 2 pins [form="♂ (male)"]
  R14 = Resistor [tolerance=±5% resistance=10k package=THT]
  J24 = Screw terminal - 2 pins [package=THT]
  J25 = male pin header, 2 pins [form="♂ (male)"]
  J26 = male pin header, 2 pins [form="♂ (male)"]
  J27 = male pin header, 2 pins [form="♂ (male)"]
  J28 = double row male pin header, 6 pins [form="♂ (male)"]

nets:
  N1: U1.A0, R1.Pin_0, J28.pin3
  N2: U1.A1, R2.Pin_0, J28.pin2
  N3: U1.A3, R3.Pin_0, J28.pin1
  N4: U1.P0, J3.pin2, J17.pin1
  N5: U1.P1, J4.pin2, J22.pin1
  N6: U1.P2, J5.pin2, J23.pin1
  N7: U1.P3, J6.pin2, J20.pin1
  N8: U1.GND, J12.pin2, R6.Pin_1, R7.Pin_0, R9.Pin_0, R10.Pin_0, R11.Pin_0, R12.Pin_0, R13.Pin_0, R14.Pin_0, J24.pin1, J25.pin1, J28.pin4, J28.pin5, J28.pin6
  N9: U1.P4, J10.pin2, J21.pin1
  N10: U1.P5, J9.pin2, J26.pin1
  N11: U1.P6, J8.pin2, J27.pin1
  N12: U1.P7, J7.pin2, J13.pin1
  N13: U1.SCL, J11.pin1, R4.Pin_1
  N14: U1.SDA, J11.pin2, R5.Pin_1
  N15: U1.VCC, R1.Pin_1, R2.Pin_1, R3.Pin_1, J12.pin1, R4.Pin_0, R5.Pin_0
  N16: J3.pin1, J4.pin1, J5.pin1, J6.pin1, J7.pin1, J8.pin1, J9.pin1, J10.pin1, J24.pin2, J25.pin2
  N17: R6.Pin_0, J17.pin2
  N18: R7.Pin_1, J20.pin2
  N19: R9.Pin_1, J22.pin2
  N20: R10.Pin_1, J21.pin2
  N21: R11.Pin_1, J26.pin2
  N22: R12.Pin_1, J27.pin2
  N23: R13.Pin_1, J13.pin2
  N24: J23.pin2, R14.Pin_1

notes:
  A0 A1 A2
  5V Gnd
  SDA
  SCL
  P0
  P1
  P2
