# Fritzing sketch alimentazione (saved by Fritzing 0.9.3b)
stripboards: 1

parts:
  D1 = P1000K [part_number=P1000K]
  D2 = P1000K [part_number=P1000K]
  D3 = P1000K [part_number=P1000K]
  J1 = screw terminal, 2 pins
  C1 = Electrolytic Capacitor [capacitance=22µF voltage=35V package="200 mil [THT, electrolytic]"]
  D4 = P1000K [part_number=P1000K]
  U1 = Voltage Regulator - Variable [package="TO220 [THT]"]
  Q1 = NPN-Transistor [package="TO92 [THT]"]
  J2 = Screw terminal - 2 pins [package=THT]
  R1 = Resistor [tolerance=±5% resistance=220 package=THT]
  R2 = Resistor [tolerance=±5% resistance=100 package=THT]
  R3 = Resistor [tolerance=±5% resistance=2.2 package=THT]
  R4 = Trimmer Potentiometer [maximum_resistance=4.7kΩ package=THT]
  D5 = Rectifier Diode [part_number=1N4001 package="300 mil [THT]"]
  U2 = Voltage Regulator - 5V [package="DPak [SMD]"]
  C2 = Electrolytic Capacitor [capacitance=100nF voltage=16V package="100 mil [THT, electrolytic]"]
  C3 = Electrolytic Capacitor [capacitance=100nF voltage=16V package="100 mil [THT, electrolytic]"]
  U3 = Voltage Regulator - Variable [package="TO220 [THT]"]
  J3 = Screw terminal - 2 pins [package=THT]
  R5 = Trimmer Potentiometer [maximum_resistance=4.7kΩ package=THT]
  R6 = Resistor [tolerance=±5% resistance=220 package=THT]
  D6 = Rectifier Diode [part_number=1N4001 package="300 mil [THT]"]
  J4 = Screw terminal - 2 pins [package=THT]
  D7 = Rectifier Diode [part_number=1N4001 package="300 mil [THT]"]

nets:
  N1: D1.cathode, D3.anode, J1.pin1
  N2: D1.anode, C1.-, D4.anode, J2.pin2, R2.Pin_0, R3.Pin_0, R4.leg1, R4.wiper, U2.GND, C2.-, C3.-, J3.pin2, R5.leg1, R5.wiper, J4.pin2
  N3: D2.cathode, D3.cathode, C1.+, U1.IN, U3.IN
  N4: D2.anode, J1.pin2, D4.cathode
  N5: U1.ADJ, R1.Pin_1, R4.leg2
  N6: U1.OUT, R1.Pin_0, D5.anode
  N7: Q1.E, R3.Pin_1
  N8: Q1.B, R2.Pin_1
  N9: Q1.C, R5.leg2, R6.Pin_1
  N10: J2.pin1, D5.cathode, U2.input_voltage, C3.+, D7.cathode
  N11: U2.output_voltage, C2.+, J3.pin1
  N12: U3.OUT, R6.Pin_0, D6.anode
  N13: D6.cathode, J4.pin1, D7.anode

notes:
  -  +
  ~  ~
  -  +    -  +
  13.8V | 5V
