# Fritzing sketch baseBoard1284 (saved by Fritzing 0.9.10b)
perfboards: 1

parts:
  Atmega1 = ATmega644 [package=pdpi]
  XTAL1 = Crystal [frequency="16 Mhz" package=THT]
  J_FTDI = female pin header, 5 pins [form="♀ (female)"]
  J_SPK = female pin header, 2 pins [form="♀ (female)"]
  J_LED = female pin header, 6 pins [form="♀ (female)"]
  GSM_SIM_GPSR_SMS_SIM900_SIM1 = SIM800L [package=THT]  # not connected
  J_GSM = female pin header, 7 pins [form="♀ (female)"]
  C1 = Ceramic Capacitor [capacitance=20pF package="100 mil [THT, multilayer]"]
  C2 = Ceramic Capacitor [capacitance=20pF package="100 mil [THT, multilayer]"]
  C3 = Ceramic Capacitor [capacitance=100nF voltage=35V package="100 mil [THT, multilayer]"]
  C4 = Ceramic Capacitor [capacitance=100nF voltage=35V package="100 mil [THT, multilayer]"]
  J1 = Screw terminal - 2 pins [package=THT]
  S1 = Pushbutton [package="[THT]"]
  Q1 = NPN-Transistor [package="TO92 [THT]"]
  R1 = Resistor [tolerance=±5% resistance=220 power=0.25 package=THT]
  R2 = Resistor [tolerance=±5% resistance=220 power=0.25 package=THT]
  R3 = Resistor [tolerance=±5% resistance=220 power=0.25 package=THT]
  R4 = Resistor [tolerance=±5% resistance=220 power=0.25 package=THT]
  C5 = Ceramic Capacitor [capacitance=100nF package="100 mil [THT, multilayer]"]
  LED1 = LED - 5mm [color="Green (555nm)" current=0.030 package="5 mm [THT]"]
  LED2 = LED - 5mm [color="Red (633nm)" current=0.030 package="5 mm [THT]"]
  LED3 = LED - 5mm [color="Yellow (595nm)" current=0.030 package="5 mm [THT]"]
  KY-1 = Keyes Relay [package=THT]  # not connected
  R5 = Resistor [tolerance=±5% resistance=220 power=0.25 package=THT]
  J_I2C = screw terminal, 4 pins

nets:
  N1: Atmega1.PB1, R3.Pin_0
  N2: Atmega1.PB2, R2.Pin_0
  N3: Atmega1.PB3, R4.Pin_0
  N4: Atmega1.RESET, Atmega1.GND, J_FTDI.pin1, J_SPK.pin1, J_LED.pin2, J_LED.pin4, J_LED.pin6, C1.0, C2.1, C3.1, C4.1, J1.pin2, S1.Pin_1, S1.Pin_2, C5.0, LED1.cathode, LED2.cathode, LED3.cathode, R5.Pin_0, J_I2C.pin3
  N5: Atmega1.VCC, C3.0, J1.pin1, Q1.C, R5.Pin_1, J_I2C.pin4
  N6: Atmega1.XTAL2, XTAL1.pin_1, C1.1
  N7: Atmega1.XTAL1, XTAL1.pin_0, C2.0
  N8: Atmega1.PD0, J_FTDI.pin3
  N9: Atmega1.PD1, J_FTDI.pin4
  N10: Atmega1.PD2, J_GSM.pin4
  N11: Atmega1.PD3, J_GSM.pin3
  N12: Atmega1.PD5, R1.Pin_1
  N13: Atmega1.PC0, J_I2C.pin1
  N14: Atmega1.PC1, J_I2C.pin2
  N15: Atmega1.AVCC, C4.0
  N16: J_FTDI.pin5, C5.1
  N17: J_SPK.pin2, Q1.E
  N18: J_LED.pin1, R3.Pin_1, LED3.anode
  N19: J_LED.pin3, R2.Pin_1, LED1.anode
  N20: J_LED.pin5, R4.Pin_1, LED2.anode
  N21: S1.Pin_3, S1.Pin_4
  N22: Q1.B, R1.Pin_0

custom parts:
  Keyes Relay: The Keyes 5V relay module is suitable for SCM development, home appliance control. It uses a 5V~12V TIL control signal which can control DC / AC signal.
