# Fritzing sketch baseBoard1284_new (saved by Fritzing 0.9.10b)
stripboards: 1
perfboards: 1

parts:
  R6 = Resistor [tolerance=±5% resistance=10k power=0.25 package=THT]
  S2 = Pushbutton [package="[THT]"]
  R7 = Resistor [tolerance=±5% resistance=220 power=0.25 package=THT]
  R8 = Resistor [tolerance=±5% resistance=220 power=0.25 package=THT]
  C6 = Ceramic Capacitor [capacitance=100nF package="100 mil [THT, multilayer]"]
  C7 = Ceramic Capacitor [capacitance=100nF package="100 mil [THT, multilayer]"]
  XTAL2 = Crystal [frequency="16 Mhz" package=THT]
  C8 = Ceramic Capacitor [capacitance=22pF package="100 mil [THT, multilayer]"]
  C9 = Ceramic Capacitor [capacitance=22pF package="100 mil [THT, multilayer]"]
  J3 = Screw terminal - 2 pins [package=THT]
  J_FTDI1 = female pin header, 5 pins [form="♀ (female)"]
  J5 = Screw terminal - 2 pins [package=THT]
  C10 = Ceramic Capacitor [capacitance=100nF package="100 mil [THT, multilayer]"]
  Q2 = NPN-Transistor [package="TO92 [THT]"]
  R10 = Resistor [tolerance=±5% resistance=220 power=0.25 package=THT]
  JRelay = female pin header, 3 pins [form="♀ (female)"]
  JSPK1 = female pin header, 2 pins [form="♀ (female)"]
  R11 = Resistor [tolerance=±5% resistance=220 power=0.25 package=THT]
  JLED = female pin header, 5 pins [form="♀ (female)"]
  R12 = Resistor [tolerance=±5% resistance=10k power=0.25 package=THT]
  R13 = Resistor [tolerance=±5% resistance=10k power=0.25 package=THT]
  JLCD = female pin header, 4 pins [form="♀ (female)"]
  R14 = Resistor [tolerance=±5% resistance=10k power=0.25 package=THT]
  R15 = Resistor [tolerance=±5% resistance=10k power=0.25 package=THT]
  R16 = Resistor [tolerance=±5% resistance=10k power=0.25 package=THT]
  JKeyPad = female pin header, 8 pins [form="♀ (female)"]
  Atmega1 = ATmega644 [package=pdpi]
  R17 = Resistor [tolerance=±5% resistance=220 power=0.25 package=THT]
  R18 = Resistor [tolerance=±5% resistance=220 power=0.25 package=THT]
  LED1 = LED - 3mm [color="Red (633nm)" current=0.030 package="3 mm [THT]"]
  J29 = Screw terminal - 2 pins [package=THT]
  J32 = Screw terminal - 2 pins [package=THT]
  J33 = Screw terminal - 2 pins [package=THT]
  J34 = Screw terminal - 2 pins [package=THT]
  J35 = Screw terminal - 2 pins [package=THT]
  J36 = Screw terminal - 2 pins [package=THT]
  J37 = Screw terminal - 2 pins [package=THT]
  J38 = Screw terminal - 2 pins [package=THT]
  J39 = Screw terminal - 2 pins [package=THT]
  J40 = male pin header, 2 pins [form="♂ (male)"]
  J41 = male pin header, 2 pins [form="♂ (male)"]
  J42 = male pin header, 2 pins [form="♂ (male)"]
  J43 = male pin header, 2 pins [form="♂ (male)"]
  J44 = male pin header, 2 pins [form="♂ (male)"]
  J45 = male pin header, 2 pins [form="♂ (male)"]
  J46 = male pin header, 2 pins [form="♂ (male)"]
  J47 = male pin header, 2 pins [form="♂ (male)"]
  R19 = Resistor [tolerance=±5% resistance=10k power=0.25 package=THT]
  R20 = Resistor [tolerance=±5% resistance=10k power=0.25 package=THT]
  R21 = Resistor [tolerance=±5% resistance=10k power=0.25 package=THT]
  R22 = Resistor [tolerance=±5% resistance=10k power=0.25 package=THT]
  R23 = Resistor [tolerance=±5% resistance=10k power=0.25 package=THT]
  R24 = Resistor [tolerance=±5% resistance=10k power=0.25 package=THT]
  R25 = Resistor [tolerance=±5% resistance=10k power=0.25 package=THT]
  R26 = Resistor [tolerance=±5% resistance=10k power=0.25 package=THT]
  R27 = Resistor [tolerance=±5% resistance=10k power=0.25 package=THT]
  R28 = Resistor [tolerance=±5% resistance=10k power=0.25 package=THT]
  R29 = Resistor [tolerance=±5% resistance=10k power=0.25 package=THT]
  R30 = Resistor [tolerance=±5% resistance=10k power=0.25 package=THT]
  R31 = Resistor [tolerance=±5% resistance=10k power=0.25 package=THT]
  J48 = male pin header, 2 pins [form="♂ (male)"]
  J49 = double row male pin header, 6 pins [form="♂ (male)"]
  J50 = double row male pin header, 6 pins [form="♂ (male)"]
  R32 = Resistor [tolerance=±5% resistance=220 power=0.25 package=THT]
  LED2 = LED - 3mm [color="Green (555nm)" current=0.030 package="3 mm [THT]"]
  J51 = Screw terminal - 2 pins [package=THT]
  J52 = Screw terminal - 2 pins [package=THT]
  J53 = Screw terminal - 2 pins [package=THT]
  JTIMER = female pin header, 6 pins [form="♀ (female)"]  # not connected
  JMOD433 = female pin header, 4 pins [form="♀ (female)"]  # not connected
  U1 = PCF8574 [package="DIP16 [THT]"]
  U2 = PCF8574 [package="DIP16 [THT]"]

nets:
  N1: R6.Pin_0, C10.0, Atmega1.RESET
  VCC: R6.Pin_1, C6.0, C7.0, J_FTDI1.pin2, J5.pin2, Q2.C, JRelay.pin1, R12.Pin_1, R13.Pin_1, JLCD.pin1, R14.Pin_1, R15.Pin_1, R16.Pin_1, Atmega1.VCC, Atmega1.AVCC, Atmega1.AREF, R18.Pin_0, R23.Pin_0, R24.Pin_0, R25.Pin_1, R26.Pin_1, R31.Pin_1, U1.VCC, U2.VCC
  GND: S2.Pin_1, S2.Pin_2, C6.1, C7.1, C8.1, C9.1, J_FTDI1.pin1, J5.pin1, JRelay.pin2, JSPK1.pin1, JLED.pin1, JLCD.pin2, Atmega1.GND, LED1.cathode, J29.pin1, J48.pin1, J50.pin4, J50.pin5, J50.pin6, LED2.cathode, U1.GND
  N2: S2.Pin_3, S2.Pin_4, Atmega1.PB7
  N3: R7.Pin_0, Atmega1.PB1
  N4: R7.Pin_1, JLED.pin2
  N5: R8.Pin_0, Atmega1.PB2
  N6: R8.Pin_1, JLED.pin3
  N7: XTAL2.pin_0, C9.0, Atmega1.XTAL1
  N8: XTAL2.pin_1, C8.0, Atmega1.XTAL2
  N9: J3.pin1, R13.Pin_0, JLCD.pin4, Atmega1.PC0, R24.Pin_1, J51.pin1, J52.pin1, J53.pin1, U1.SCL, U2.SCL
  N10: J3.pin2, R12.Pin_0, JLCD.pin3, Atmega1.PC1, R23.Pin_1, J51.pin2, J52.pin2, J53.pin2, U1.SDA, U2.SDA
  N11: J_FTDI1.pin3, Atmega1.PD0
  N12: J_FTDI1.pin4, Atmega1.PD1
  N13: J_FTDI1.pin5, C10.1
  N14: Q2.E, JSPK1.pin2
  N15: Q2.B, R10.Pin_1
  N16: R10.Pin_0, Atmega1.PD5
  N17: JRelay.pin3, Atmega1.PD6
  N18: R11.Pin_0, Atmega1.PB4
  N19: R11.Pin_1, JLED.pin5
  N20: JLED.pin4, R17.Pin_1
  N21: R14.Pin_0, J50.pin1, U1.A2
  N22: R15.Pin_0, J50.pin2, U1.A1
  N23: R16.Pin_0, J50.pin3, U1.A0
  N24: JKeyPad.pin1, U1.P4
  N25: JKeyPad.pin2, U1.P5
  N26: JKeyPad.pin3, U1.P6
  N27: JKeyPad.pin4, U1.P7
  N28: JKeyPad.pin5, U1.P0
  N29: JKeyPad.pin6, U1.P1
  N30: JKeyPad.pin7, U1.P2
  N31: JKeyPad.pin8, U1.P3
  N32: Atmega1.PB0, R32.Pin_0
  N33: Atmega1.PB3, R17.Pin_0
  N34: R18.Pin_1, LED1.anode
  N35: J29.pin2, J32.pin1, J33.pin1, J34.pin1, J35.pin1, J36.pin1, J37.pin1, J38.pin1, J39.pin1, J48.pin2
  N36: J32.pin2, J46.pin1, U2.P4
  N37: J33.pin2, J44.pin1, U2.P5
  N38: J34.pin2, J45.pin1, U2.P6
  N39: J35.pin2, J47.pin1, U2.P7
  N40: J36.pin2, J40.pin1, U2.P3
  N41: J37.pin2, J43.pin1, U2.P2
  N42: J38.pin2, J42.pin1, U2.P1
  N43: J39.pin2, J41.pin1, U2.P0
  N44: J40.pin2, R21.Pin_1
  N45: J41.pin2, R22.Pin_0
  N46: J42.pin2, R19.Pin_1
  N47: J43.pin2, R20.Pin_1
  N48: J44.pin2, R29.Pin_1
  N49: J45.pin2, R28.Pin_1
  N50: J46.pin2, R30.Pin_1
  N51: J47.pin2, R27.Pin_1
  N52: R19.Pin_0, R20.Pin_0, R21.Pin_0, R22.Pin_1, R27.Pin_0, R28.Pin_0, R29.Pin_0, R30.Pin_0, J49.pin4, J49.pin5, J49.pin6, U2.GND
  N53: R25.Pin_0, J49.pin1, U2.A2
  N54: R26.Pin_0, J49.pin2, U2.A1
  N55: R31.Pin_0, J49.pin3, U2.A0
  N56: R32.Pin_1, LED2.anode

notes:
  SCL
  SDA
  Relay
  Spk
  LedAttivato
  LedDisattivo
  LedAnomalie
  LedMonSirena
  LCD
  A0 A1 A2
  5V Gnd
  P2
  P1
  P0
