# Fritzing sketch sirena (saved by Fritzing 0.9.2b)
perfboards: 1

parts:
  J2 = Piezo Speaker
  J1 = screw terminal, 6 pins
  U1 = 2-Channel 5v Relay Shield [package=relay-2ch5v10a]

nets:
  N1: J2.pin1, J1.pin6
  N2: J2.pin2, J1.pin4, J1.pin5, U1.K1-Off
  N3: J1.pin2, J1.pin3, U1.K1-In

notes:
  Vin 13.8
  Gnd
  Sirena +

custom parts:
  2-Channel 5v Relay Shield: 2 Channel 5v Relay Shield w. 2x SPD-06VDC-SD-C
